# Fritzing sketch attiny-usbtinyISP (saved by Fritzing 0.9.3b)
breadboards: 1

parts:
  U1 = attiny85 [package=dip]
  J1 = AVR ISP 6 Pin [package=2x3-ns]

nets:
  N1: U1.Pin_1, J1.5
  N2: U1.Pin_4, J1.6
  N3: U1.Pin_5, J1.4
  N4: U1.Pin_6, J1.1
  N5: U1.Pin_7, J1.3
  N6: U1.Pin_8, J1.2
