# Fritzing sketch bare-atmega-breadboard-ftdi (saved by Fritzing 0.9.3b)
breadboards: 1

parts:
  U1 = atmega328 [package=dip]
  R1 = Resistor [tolerance=±5% resistance=330 package=THT]
  LED1 = LED - 5mm [color="Red (633nm)" package="5 mm [THT]"]
  R2 = Resistor [tolerance=±5% resistance=10k package=THT]
  R4 = Resistor [tolerance=±5% resistance=10k package=THT]
  R3 = Resistor [tolerance=±5% resistance=10k package=THT]
  Part1 = FTDI Basic Programmer
  C1 = Electrolytic Capacitor [capacitance=0.1µF package="100 mil [THT, electrolytic]"]

nets:
  N1: U1.RESET, R2.Pin_0, C1.+
  N2: U1.D0_(RX), R3.Pin_0, Part1.RXI
  N3: U1.D1_(TX), R4.Pin_0, Part1.TXO
  N4: U1.VCC, R2.Pin_1, R4.Pin_1, R3.Pin_1, Part1.POWER
  N5: U1.GND#7, Part1.GND
  N6: U1.D13, R1.Pin_0
  N7: U1.GND#21, LED1.cathode
  N8: R1.Pin_1, LED1.anode
  N9: Part1.DTR, C1.-
