# Fritzing sketch bare-atmega-breadboard (saved by Fritzing 0.9.3b)
breadboards: 1

parts:
  U1 = atmega328 [package=dip]
  R1 = Resistor [tolerance=±5% resistance=330 package=THT]
  LED1 = LED - 5mm [color="Red (633nm)" package="5 mm [THT]"]
  R2 = Resistor [tolerance=±5% resistance=10k package=THT]
  J1 = AVR ISP 6 Pin [package=2x3]
  Part1 = FTDI Basic Programmer  # not connected

nets:
  N1: U1.RESET, R2.Pin_0, J1.5
  N2: U1.VCC, R2.Pin_1
  N3: U1.D11_(PWM), J1.4
  N4: U1.D12, J1.1
  N5: U1.D13, R1.Pin_0, J1.3
  N6: U1.AVCC, J1.2
  N7: U1.GND#21, LED1.cathode, J1.6
  N8: R1.Pin_1, LED1.anode
